// Logisim project circuito_completo.circ as structural Verilog: 7 circuits, main circuit main
module main (
  input  [7:0] B,
  input  [7:0] A,
  input  [2:0] Operation,
  input  Cin,
  output ESTOURO
);

  wire n6_circuito_de_controle_segmentos_do_display_1_a, n6_circuito_de_controle_segmentos_do_display_1_b,
       n6_circuito_de_controle_segmentos_do_display_1_c, n6_circuito_de_controle_segmentos_do_display_1_d,
       n6_circuito_de_controle_segmentos_do_display_1_e, n6_circuito_de_controle_segmentos_do_display_1_f,
       n6_circuito_de_controle_segmentos_do_display_1_g, n6_circuito_de_controle_segmentos_do_display_2_a,
       n6_circuito_de_controle_segmentos_do_display_2_b, n6_circuito_de_controle_segmentos_do_display_2_c,
       n6_circuito_de_controle_segmentos_do_display_2_d, n6_circuito_de_controle_segmentos_do_display_2_e,
       n6_circuito_de_controle_segmentos_do_display_2_f, n6_circuito_de_controle_segmentos_do_display_2_g,
       n6_circuito_de_controle_segmentos_do_display_3_a, n6_circuito_de_controle_segmentos_do_display_3_b,
       n6_circuito_de_controle_segmentos_do_display_3_c, n6_circuito_de_controle_segmentos_do_display_3_d,
       n6_circuito_de_controle_segmentos_do_display_3_e, n6_circuito_de_controle_segmentos_do_display_3_f,
       n6_circuito_de_controle_segmentos_do_display_3_g;
  wire [7:0] DIVISOR_centena, DIVISOR_dezena, DIVISOR_unidade;

  _5___DIVISOR DIVISOR (
    .B(B), .Cout(ESTOURO), .A(A), .Operation(Operation), .Cin(Cin), .CENTENA(DIVISOR_centena),
    .DEZENA(DIVISOR_dezena), .UNIDADE(DIVISOR_unidade));
  _7_Segment_Display u_7_segment_display_1 (
    .g(n6_circuito_de_controle_segmentos_do_display_1_g),
    .f(n6_circuito_de_controle_segmentos_do_display_1_f),
    .a(n6_circuito_de_controle_segmentos_do_display_1_a),
    .b(n6_circuito_de_controle_segmentos_do_display_1_b),
    .e(n6_circuito_de_controle_segmentos_do_display_1_e),
    .d(n6_circuito_de_controle_segmentos_do_display_1_d), .c(n6_circuito_de_controle_segmentos_do_display_1_c));  // open: dp
  _6___CIRCUITO_DE_CONTROLE_SEGMENTOS_DO_DISPLAY u_6_circuito_de_controle_segmentos_do_display_1 (
    .a(n6_circuito_de_controle_segmentos_do_display_1_a),
    .b(n6_circuito_de_controle_segmentos_do_display_1_b),
    .c(n6_circuito_de_controle_segmentos_do_display_1_c),
    .d(n6_circuito_de_controle_segmentos_do_display_1_d),
    .e(n6_circuito_de_controle_segmentos_do_display_1_e),
    .f(n6_circuito_de_controle_segmentos_do_display_1_f),
    .g(n6_circuito_de_controle_segmentos_do_display_1_g), ._3__A(DIVISOR_centena[3]),
    ._2__B(DIVISOR_centena[2]), ._1__C(DIVISOR_centena[1]), ._0__D(DIVISOR_centena[0]));
  _6___CIRCUITO_DE_CONTROLE_SEGMENTOS_DO_DISPLAY u_6_circuito_de_controle_segmentos_do_display_2 (
    .a(n6_circuito_de_controle_segmentos_do_display_2_a),
    .b(n6_circuito_de_controle_segmentos_do_display_2_b),
    .c(n6_circuito_de_controle_segmentos_do_display_2_c),
    .d(n6_circuito_de_controle_segmentos_do_display_2_d),
    .e(n6_circuito_de_controle_segmentos_do_display_2_e),
    .f(n6_circuito_de_controle_segmentos_do_display_2_f),
    .g(n6_circuito_de_controle_segmentos_do_display_2_g), ._3__A(DIVISOR_dezena[3]),
    ._2__B(DIVISOR_dezena[2]), ._1__C(DIVISOR_dezena[1]), ._0__D(DIVISOR_dezena[0]));
  _7_Segment_Display u_7_segment_display_2 (
    .g(n6_circuito_de_controle_segmentos_do_display_2_g),
    .f(n6_circuito_de_controle_segmentos_do_display_2_f),
    .a(n6_circuito_de_controle_segmentos_do_display_2_a),
    .b(n6_circuito_de_controle_segmentos_do_display_2_b),
    .e(n6_circuito_de_controle_segmentos_do_display_2_e),
    .d(n6_circuito_de_controle_segmentos_do_display_2_d), .c(n6_circuito_de_controle_segmentos_do_display_2_c));  // open: dp
  _7_Segment_Display u_7_segment_display_3 (
    .g(n6_circuito_de_controle_segmentos_do_display_3_g),
    .f(n6_circuito_de_controle_segmentos_do_display_3_f),
    .a(n6_circuito_de_controle_segmentos_do_display_3_a),
    .b(n6_circuito_de_controle_segmentos_do_display_3_b),
    .e(n6_circuito_de_controle_segmentos_do_display_3_e),
    .d(n6_circuito_de_controle_segmentos_do_display_3_d), .c(n6_circuito_de_controle_segmentos_do_display_3_c));  // open: dp
  _6___CIRCUITO_DE_CONTROLE_SEGMENTOS_DO_DISPLAY u_6_circuito_de_controle_segmentos_do_display_3 (
    .a(n6_circuito_de_controle_segmentos_do_display_3_a),
    .b(n6_circuito_de_controle_segmentos_do_display_3_b),
    .c(n6_circuito_de_controle_segmentos_do_display_3_c),
    .d(n6_circuito_de_controle_segmentos_do_display_3_d),
    .e(n6_circuito_de_controle_segmentos_do_display_3_e),
    .f(n6_circuito_de_controle_segmentos_do_display_3_f),
    .g(n6_circuito_de_controle_segmentos_do_display_3_g), ._3__A(DIVISOR_unidade[3]),
    ._2__B(DIVISOR_unidade[2]), ._1__C(DIVISOR_unidade[1]), ._0__D(DIVISOR_unidade[0]));

  // Notes on the sheet:
  //   0 - AND
  //   1 - OR
  //   2 - NAND
  //   3 - NOR
  //   4 - NOT (A)
  //   5 - XOR
  //   6 - SOMA
  //   7 - SUBTRAÇÃO
  //   MENU  
  //   Colocar código no campo "Operation"
  //   O quarto é a replicação do terceiro 8 vezes, para ser possivel trabalhar com 8 bits
  //   CIRCUITO COMPLETO
  //   CENTENA
  //   O circuito é resultado da integração dos demais que estão enumerados de 1 a 6 neste mesmo arquivo. 
  //   O terceiro representa uma ULA com todas as operações, com o decoder incluso, mas para 1 bit
  //   Como a finalidade é representar em display de 7 segmentos, é necessário separar dezena, centena e unidade.
  //   O sexto componente trabalha com os 4 primeiros bits do resultado da divisão para ativação dos segmentos no display
  //   DEZENA
  //   O primeiro (decoder) é responsável por escolher a operação a ser realizada. O número 2 representa o somador e subtrator completo. 
  //   UNIDADE
endmodule

// DECODER
module _1___DECODER (
  input  A,
  input  B,
  input  C,
  output out_4,
  output out_5,
  output out_6,
  output out_7,
  output out_8,
  output out_9,
  output sub_soma,
  output out_11
);

  wire not_1_out, not_2_out, not_3_out, SOMA_out, SUB_out;

  not not_1 (not_1_out, A);
  not not_2 (not_2_out, B);
  not not_3 (not_3_out, C);
  and AND (out_4, not_1_out, not_2_out, not_3_out);
  and OR (out_5, not_1_out, not_2_out, C);
  and NAND (out_6, not_1_out, B, not_3_out);
  and NOR (out_7, not_1_out, B, C);
  and NOT_4 (out_8, A, not_2_out, not_3_out);
  and XOR (out_9, A, not_2_out, C);
  and SOMA (SOMA_out, A, B);
  and SUB (SUB_out, B, A);
  or or_2 (out_11, SOMA_out, SUB_out);

  assign sub_soma = C;

  // Notes on the sheet:
  //   SELETOR DE OPERAÇÃO
endmodule

module _3___ULA_1_BIT (
  input  Cin,
  input  A,
  input  B,
  input  C1,
  input  C2,
  input  C3,
  output S,
  output Cout
);

  wire and_1_out, AND_2_out, n1_decoder_1_out_4, n1_decoder_1_out_5, n1_decoder_1_out_6, n1_decoder_1_out_7,
       n1_decoder_1_out_8, n1_decoder_1_out_9, n1_decoder_1_out_11, n1_decoder_1_sub_soma,
       n2_somador_subtrator_1_out_6, nand_1_out, NAND_2_out, nor_1_out, NOR_2_out, not_1_out, NOT_2_out,
       or_1_out, OR_2_out, or_3_out, xor_1_out, XOR_2_out;

  _1___DECODER u_1_decoder_1 (
    .A(C1), .B(C2), .C(C3), .out_4(n1_decoder_1_out_4), .out_5(n1_decoder_1_out_5),
    .out_6(n1_decoder_1_out_6), .out_7(n1_decoder_1_out_7), .out_8(n1_decoder_1_out_8),
    .out_9(n1_decoder_1_out_9), .sub_soma(n1_decoder_1_sub_soma), .out_11(n1_decoder_1_out_11));
  and and_1 (and_1_out, B, A);
  or or_1 (or_1_out, A, B);
  nand nand_1 (nand_1_out, A, B);
  nor nor_1 (nor_1_out, A, B);
  not not_1 (not_1_out, A);
  xor xor_1 (xor_1_out, A, B);
  and AND_2 (AND_2_out, and_1_out, n1_decoder_1_out_4);
  and OR_2 (OR_2_out, or_1_out, n1_decoder_1_out_5);
  and NAND_2 (NAND_2_out, nand_1_out, n1_decoder_1_out_6);
  and NOR_2 (NOR_2_out, nor_1_out, n1_decoder_1_out_7);
  and NOT_2 (NOT_2_out, not_1_out, n1_decoder_1_out_8);
  and XOR_2 (XOR_2_out, xor_1_out, n1_decoder_1_out_9);
  _2___SOMADOR_SUBTRATOR u_2_somador_subtrator_1 (
    .A(A), .B(B), .Cin(Cin), .C3(n1_decoder_1_sub_soma), .ON_OFF(n1_decoder_1_out_11), .Cout(Cout),
    .out_6(n2_somador_subtrator_1_out_6));
  or or_3 (or_3_out, AND_2_out, OR_2_out, NAND_2_out, NOR_2_out, NOT_2_out);
  or or_4 (S, or_3_out, XOR_2_out, n2_somador_subtrator_1_out_6);

  // Notes on the sheet:
  //   REALIZA OPERAÇÕES COM APENAS 1 BIT
endmodule

// + / -
module _2___SOMADOR_SUBTRATOR (
  input  A,
  input  B,
  input  Cin,
  input  C3,
  input  ON_OFF,
  output out_6,
  output Cout
);

  wire and_1_out, and_2_out, or_1_out, or_2_out, xor_1_out, xor_2_out, xor_3_out;

  xor xor_1 (xor_1_out, C3, A);
  and and_1 (and_1_out, xor_1_out, or_1_out);
  or or_1 (or_1_out, B, Cin);
  and and_2 (and_2_out, Cin, B);
  or or_2 (or_2_out, and_1_out, and_2_out);
  and and_3 (Cout, or_2_out, ON_OFF);
  xor xor_2 (xor_2_out, A, B);
  xor xor_3 (xor_3_out, xor_2_out, Cin);
  and and_4 (out_6, xor_3_out, ON_OFF);

  // Notes on the sheet:
  //   CIRCUITO SOMADOR/SUBTRATOR COMPLETO PARA SER INTEGRADO À ULA
endmodule

module _4___ULA_8_BITS (
  input  [7:0] B,
  input  [7:0] A,
  input  [2:0] control,
  input  Cin,
  output Cout,
  output [7:0] \RESULTADO_OPERAÇÃO 
);

  wire n3_ula_1_bit_2_cout, n3_ula_1_bit_3_cout, n3_ula_1_bit_4_cout, n3_ula_1_bit_5_cout,
       n3_ula_1_bit_6_cout, n3_ula_1_bit_7_cout, n3_ula_1_bit_8_cout;

  _3___ULA_1_BIT u_3_ula_1_bit_1 (
    .A(A[7]), .B(B[7]), .C1(control[2]), .C2(control[1]), .C3(control[0]), .Cin(n3_ula_1_bit_2_cout),
    .Cout(Cout), .S(\RESULTADO_OPERAÇÃO [7]));
  _3___ULA_1_BIT u_3_ula_1_bit_2 (
    .A(A[6]), .B(B[6]), .C1(control[2]), .C2(control[1]), .C3(control[0]), .Cin(n3_ula_1_bit_3_cout),
    .Cout(n3_ula_1_bit_2_cout), .S(\RESULTADO_OPERAÇÃO [6]));
  _3___ULA_1_BIT u_3_ula_1_bit_3 (
    .A(A[5]), .B(B[5]), .C1(control[2]), .C2(control[1]), .C3(control[0]), .Cin(n3_ula_1_bit_4_cout),
    .Cout(n3_ula_1_bit_3_cout), .S(\RESULTADO_OPERAÇÃO [5]));
  _3___ULA_1_BIT u_3_ula_1_bit_4 (
    .A(A[4]), .B(B[4]), .C1(control[2]), .C2(control[1]), .C3(control[0]), .Cin(n3_ula_1_bit_5_cout),
    .Cout(n3_ula_1_bit_4_cout), .S(\RESULTADO_OPERAÇÃO [4]));
  _3___ULA_1_BIT u_3_ula_1_bit_5 (
    .A(A[3]), .B(B[3]), .C1(control[2]), .C2(control[1]), .C3(control[0]), .Cin(n3_ula_1_bit_6_cout),
    .Cout(n3_ula_1_bit_5_cout), .S(\RESULTADO_OPERAÇÃO [3]));
  _3___ULA_1_BIT u_3_ula_1_bit_6 (
    .A(A[2]), .B(B[2]), .C1(control[2]), .C2(control[1]), .C3(control[0]), .Cin(n3_ula_1_bit_7_cout),
    .Cout(n3_ula_1_bit_6_cout), .S(\RESULTADO_OPERAÇÃO [2]));
  _3___ULA_1_BIT u_3_ula_1_bit_7 (
    .A(A[1]), .B(B[1]), .C1(control[2]), .C2(control[1]), .C3(control[0]), .Cin(n3_ula_1_bit_8_cout),
    .Cout(n3_ula_1_bit_7_cout), .S(\RESULTADO_OPERAÇÃO [1]));
  _3___ULA_1_BIT u_3_ula_1_bit_8 (
    .A(A[0]), .B(B[0]), .C1(control[2]), .C2(control[1]), .C3(control[0]), .Cin(Cin),
    .Cout(n3_ula_1_bit_8_cout), .S(\RESULTADO_OPERAÇÃO [0]));

  // Notes on the sheet:
  //   REALIZA TODAS AS OPERAÇÕES PREVISTAS COM, NO MÁXIMO, 8 BITS
endmodule

module _5___DIVISOR (
  input  [7:0] B,
  input  [7:0] A,
  input  [2:0] Operation,
  input  Cin,
  output Cout,
  output [7:0] CENTENA,
  output [7:0] DEZENA,
  output [7:0] UNIDADE
);

  wire [7:0] divider_1_rem, divider_2_rem, \n4_ula_8_bits_1_resultado_operação ;

  _4___ULA_8_BITS u_4_ula_8_bits_1 (
    .Cout(Cout), .control(Operation), .\RESULTADO_OPERAÇÃO (\n4_ula_8_bits_1_resultado_operação ), .B(B),
    .A(A), .Cin(Cin));
  Divider divider_1 (
    .a(\n4_ula_8_bits_1_resultado_operação ), .b(8'h64), .out(CENTENA), .rem(divider_1_rem));  // open: upper
  Divider divider_2 (.a(divider_1_rem), .b(8'ha), .out(DEZENA), .rem(divider_2_rem));  // open: upper
  Divider divider_3 (.a(divider_2_rem), .b(8'h1), .out(UNIDADE));  // open: upper, rem

  // Notes on the sheet:
  //   DIVISOR: APÓS A OPERAÇÃO NA ULA FRACIONA O VALOR DE 8 BITS EM UNIDADE, DEZENA E CENTENA PARA EXIBIÇÃO NO DISPLAY DE SETE SEGMENTOS
endmodule

module _6___CIRCUITO_DE_CONTROLE_SEGMENTOS_DO_DISPLAY (
  input  _3__A,
  input  _2__B,
  input  _1__C,
  input  _0__D,
  output a,
  output b,
  output c,
  output d,
  output e,
  output f,
  output g
);

  wire and_1_out, and_2_out, and_3_out, and_4_out, and_5_out, and_6_out, and_7_out, and_8_out, and_9_out,
       and_10_out, not_1_out, not_2_out, not_3_out, xnor_1_out, xnor_2_out, xor_1_out;

  not not_1 (not_1_out, _2__B);
  not not_2 (not_2_out, _1__C);
  not not_3 (not_3_out, _0__D);
  xnor xnor_1 (xnor_1_out, _0__D, _2__B);
  xnor xnor_2 (xnor_2_out, _1__C, _0__D);
  and and_1 (and_1_out, not_1_out, not_3_out);
  and and_2 (and_2_out, _1__C, not_3_out);
  and and_3 (and_3_out, not_1_out, _1__C);
  and and_4 (and_4_out, _0__D, not_2_out, _2__B);
  and and_5 (and_5_out, not_3_out, _1__C);
  and and_6 (and_6_out, not_3_out, not_1_out);
  and and_7 (and_7_out, not_3_out, not_2_out);
  and and_8 (and_8_out, not_2_out, _2__B);
  and and_9 (and_9_out, not_3_out, _2__B);
  and and_10 (and_10_out, not_3_out, _1__C);
  xor xor_1 (xor_1_out, _1__C, _2__B);
  or or_1 (a, xnor_1_out, _1__C, _3__A);
  or or_2 (b, xnor_2_out, not_1_out);
  or or_3 (c, _0__D, not_2_out, _2__B);
  or or_4 (d, and_1_out, and_2_out, and_3_out, and_4_out);
  or or_5 (e, and_5_out, and_6_out);
  or or_6 (f, and_7_out, and_8_out, and_9_out, _3__A);
  or or_7 (g, _3__A, and_10_out, xor_1_out);

  // Notes on the sheet:
  //   PORTAS QUE ATIVAM DETERMINADOS SEGMENTOS NO DISPLAY
endmodule
