// Logisim project RELOGIO.circ as structural Verilog: 3 circuits, main circuit main
module main (
  output [6:0] out_1
);

  wire clock_1_out, divisor_1_p3, divisor_1_p4, divisor_1_p5, undriven, undriven_2, undriven_3, undriven_4,
       undriven_5, undriven_6, undriven_7;
  wire [3:0] divisor_1_p1;

  Clock clock_1 (.out(clock_1_out));
  J_K_Flip_Flop j_k_ff_1 (.J(1'b1), .clk(clock_1_out), .K(1'b1), .Q(out_1[6]));  // open: Qn, preset, en, reset
  J_K_Flip_Flop j_k_ff_2 (.J(1'b1), .clk(out_1[6]), .K(1'b1), .Q(out_1[5]));  // open: Qn, preset, en, reset
  J_K_Flip_Flop j_k_ff_3 (.J(1'b1), .clk(out_1[5]), .K(1'b1), .Q(out_1[4]));  // open: Qn, preset, en, reset
  J_K_Flip_Flop j_k_ff_4 (.J(1'b1), .clk(out_1[4]), .K(1'b1), .Q(out_1[3]));  // open: Qn, preset, en, reset
  _7_Segment_Display u_7_segment_display_1 (
    .g(undriven_2), .f(divisor_1_p1[3]), .a(divisor_1_p1[2]), .b(divisor_1_p1[1]), .e(undriven),
    .d(undriven_3), .c(divisor_1_p1[0]));  // open: dp
  J_K_Flip_Flop j_k_ff_5 (.J(1'b1), .clk(out_1[3]), .K(1'b1), .Q(out_1[2]));  // open: Qn, preset, en, reset
  // divisor divisor_1: pin names not known; wires that end beside it: divisor_1_p1, out_1, divisor_1_p3, divisor_1_p4, divisor_1_p5
  _7_Segment_Display u_7_segment_display_2 (
    .g(divisor_1_p5), .f(undriven_4), .a(undriven_5), .b(undriven_6), .e(divisor_1_p4), .d(divisor_1_p3),
    .c(undriven_7));  // open: dp
  J_K_Flip_Flop j_k_ff_6 (.J(1'b1), .clk(out_1[2]), .K(1'b1), .Q(out_1[1]));  // open: Qn, preset, en, reset
  divisor divisor_2 ();  // open: DEZENA, UNIDADE, ENTRADA
  J_K_Flip_Flop j_k_ff_7 (.J(1'b1), .clk(out_1[1]), .K(1'b1), .Q(out_1[0]));  // open: Qn, preset, en, reset
endmodule

module divisor (
  input  [6:0] ENTRADA,
  output [6:0] DEZENA,
  output [6:0] UNIDADE
);

  wire [6:0] divider_1_rem;

  Divider #(.width(7)) divider_1 (.a(ENTRADA), .b(7'b0001010), .out(DEZENA), .rem(divider_1_rem));  // open: upper
  Divider #(.width(7)) divider_2 (.a(divider_1_rem), .b(7'b0000001), .out(UNIDADE));  // open: upper, rem
endmodule

module SEGUNDOS (
  input  _3__A,
  input  _2__B,
  input  _1__C,
  input  _0__D,
  output a,
  output b,
  output c,
  output d,
  output e,
  output f,
  output g
);

  wire and_1_out, and_2_out, and_3_out, and_4_out, and_5_out, and_6_out, and_7_out, and_8_out, and_9_out,
       and_10_out, not_1_out, not_2_out, not_3_out, xnor_1_out, xnor_2_out, xor_1_out;

  not not_1 (not_1_out, _2__B);
  not not_2 (not_2_out, _1__C);
  not not_3 (not_3_out, _0__D);
  xnor xnor_1 (xnor_1_out, _0__D, _2__B);
  xnor xnor_2 (xnor_2_out, _1__C, _0__D);
  and and_1 (and_1_out, not_1_out, not_3_out);
  and and_2 (and_2_out, _1__C, not_3_out);
  and and_3 (and_3_out, not_1_out, _1__C);
  and and_4 (and_4_out, _0__D, not_2_out, _2__B);
  and and_5 (and_5_out, not_3_out, _1__C);
  and and_6 (and_6_out, not_3_out, not_1_out);
  and and_7 (and_7_out, not_3_out, not_2_out);
  and and_8 (and_8_out, not_2_out, _2__B);
  and and_9 (and_9_out, not_3_out, _2__B);
  and and_10 (and_10_out, not_3_out, _1__C);
  xor xor_1 (xor_1_out, _1__C, _2__B);
  or or_1 (a, xnor_1_out, _1__C, _3__A);
  or or_2 (b, xnor_2_out, not_1_out);
  or or_3 (c, _0__D, not_2_out, _2__B);
  or or_4 (d, and_1_out, and_2_out, and_3_out, and_4_out);
  or or_5 (e, and_5_out, and_6_out);
  or or_6 (f, and_7_out, and_8_out, and_9_out, _3__A);
  or or_7 (g, _3__A, and_10_out, xor_1_out);

  // Notes on the sheet:
  //   PORTAS QUE ATIVAM DETERMINADOS SEGMENTOS NO DISPLAY
endmodule
